// Digital circuit Processor.dig as structural Verilog
module Processor (
  input  CLOCK,
  input  [2:0] BUS_OUT_ADDRESS,
  input  CLOCK_OUT
);

  wire _1s, _10s, _100s, a, b, BUS_OUT_0, BUS_OUT_6, BUS_OUT_7, c, d, dipswitch_1_out, dipswitch_2_out,
       dipswitch_3_out, dipswitch_4_out, dipswitch_5_out, dipswitch_6_out, dipswitch_7_out, dipswitch_8_out,
       dipswitch_9_out, dipswitch_10_out, e, f, g, nCLOCK, nOUT_BUS_ALUT, nOUT_BUS_PC, nOUT_BUS_RAM,
       nOUT_BUS_REGA, nOUT_BUS_REGB, OUT_1s, SIGN;
  wire [7:0] BUS, MAR_OUT, PEEK_ALU, PEEK_PC, PEEK_RAM, REG_A, REG_B;

  DipSwitch dipswitch_1 (.out(dipswitch_1_out));
  DipSwitch dipswitch_2 (.out(dipswitch_2_out));
  DipSwitch #(.dipDefault("true")) dipswitch_3 (.out(dipswitch_3_out));
  DipSwitch #(.dipDefault("true")) dipswitch_4 (.out(dipswitch_4_out));
  DipSwitch #(.dipDefault("true")) dipswitch_5 (.out(dipswitch_5_out));
  DipSwitch #(.dipDefault("true")) dipswitch_6 (.out(dipswitch_6_out));
  DipSwitch #(.dipDefault("true")) dipswitch_7 (.out(dipswitch_7_out));
  DipSwitch dipswitch_8 (.out(dipswitch_8_out));
  DipSwitch dipswitch_9 (.out(dipswitch_9_out));
  DipSwitch #(.dipDefault("true")) dipswitch_10 (.out(dipswitch_10_out));
  Stop HALT (.stop(dipswitch_1_out));
  Pc pc_1 (
    .CLOCK(nCLOCK), .COUNT(dipswitch_2_out), .BUS_nIN(dipswitch_3_out), .BUS_nOUT(nOUT_BUS_PC), .BUS(BUS),
    .PEEK(PEEK_PC));
  Ram ram_1 (
    .CLOCK(CLOCK), .ADDRESS(MAR_OUT), .nIN_BUS(dipswitch_4_out), .nOUT_BUS(nOUT_BUS_RAM), .BUS(BUS),
    .PEEK(PEEK_RAM));
  Mar mar_1 (.CLOCK(CLOCK), .BUS(BUS), .BUS_nIN(dipswitch_5_out), .OUT(MAR_OUT));
  Register u_A (.CLOCK(CLOCK), .nIN_BUS(dipswitch_6_out), .nOUT_BUS(nOUT_BUS_REGA), .BUS(BUS), .OUTPUT(REG_A));
  Register u_B (.CLOCK(CLOCK), .nIN_BUS(dipswitch_7_out), .nOUT_BUS(nOUT_BUS_REGB), .BUS(BUS), .OUTPUT(REG_B));
  Alu alu_1 (.A(REG_A), .B(REG_B), .SUBTRACT(dipswitch_8_out), .nOUT_BUS(nOUT_BUS_ALUT), .BUS(BUS), .PEEK(PEEK_ALU));
  Out out_1 (
    .CLOCK(CLOCK), .REFRESH(CLOCK_OUT), .BUS(BUS), .SIGNED(dipswitch_9_out), .nIN_BUS(dipswitch_10_out),
    .PLACE({SIGN, _100s, _10s, _1s}), .OUTPUT_7SEG({a, b, c, d, e, f, g}));
  not not_1 (nCLOCK, CLOCK);
  // Probe ~CLOCK on nCLOCK
  LED led_1 (.in(BUS[5]));
  LED led_2 (.in(BUS[6]));
  LED led_3 (.in(BUS[7]));
  LED led_4 (.in(PEEK_PC[5]));
  LED led_5 (.in(PEEK_PC[6]));
  LED led_6 (.in(PEEK_PC[7]));
  LED led_7 (.in(PEEK_RAM[5]));
  LED led_8 (.in(PEEK_RAM[6]));
  LED led_9 (.in(PEEK_RAM[7]));
  LED led_10 (.in(MAR_OUT[5]));
  LED led_11 (.in(MAR_OUT[6]));
  LED led_12 (.in(MAR_OUT[7]));
  LED led_13 (.in(REG_A[5]));
  LED led_14 (.in(REG_A[6]));
  LED led_15 (.in(REG_A[7]));
  LED led_16 (.in(REG_B[5]));
  LED led_17 (.in(REG_B[6]));
  LED led_18 (.in(REG_B[7]));
  LED led_19 (.in(PEEK_ALU[5]));
  LED led_20 (.in(PEEK_ALU[6]));
  LED led_21 (.in(PEEK_ALU[7]));
  LED led_22 (.in(BUS[1]));
  LED led_23 (.in(BUS[2]));
  LED led_24 (.in(BUS[3]));
  LED led_25 (.in(BUS[4]));
  LED led_26 (.in(PEEK_PC[1]));
  LED led_27 (.in(PEEK_PC[2]));
  LED led_28 (.in(PEEK_PC[3]));
  LED led_29 (.in(PEEK_PC[4]));
  LED led_30 (.in(PEEK_RAM[1]));
  LED led_31 (.in(PEEK_RAM[2]));
  LED led_32 (.in(PEEK_RAM[3]));
  LED led_33 (.in(PEEK_RAM[4]));
  LED led_34 (.in(MAR_OUT[1]));
  LED led_35 (.in(MAR_OUT[2]));
  LED led_36 (.in(MAR_OUT[3]));
  LED led_37 (.in(MAR_OUT[4]));
  LED led_38 (.in(REG_A[1]));
  LED led_39 (.in(REG_A[2]));
  LED led_40 (.in(REG_A[3]));
  LED led_41 (.in(REG_A[4]));
  LED led_42 (.in(REG_B[1]));
  LED led_43 (.in(REG_B[2]));
  LED led_44 (.in(REG_B[3]));
  LED led_45 (.in(REG_B[4]));
  LED led_46 (.in(PEEK_ALU[1]));
  LED led_47 (.in(PEEK_ALU[2]));
  LED led_48 (.in(PEEK_ALU[3]));
  LED led_49 (.in(PEEK_ALU[4]));
  LED led_50 (.in(BUS[0]));
  LED led_51 (.in(PEEK_PC[0]));
  LED led_52 (.in(PEEK_RAM[0]));
  LED led_53 (.in(MAR_OUT[0]));
  LED led_54 (.in(REG_A[0]));
  LED led_55 (.in(REG_B[0]));
  LED led_56 (.in(PEEK_ALU[0]));
  _74138 u_BUS_OUT_ADDRESS (
    .pin1(BUS_OUT_ADDRESS[0]), .pin2(BUS_OUT_ADDRESS[1]), .pin3(BUS_OUT_ADDRESS[2]), .pin4(1'b0),
    .pin5(1'b0), .pin6(1'b1), .pin7(BUS_OUT_7), .pin8(1'b0), .pin9(BUS_OUT_6), .pin10(nOUT_BUS_ALUT),
    .pin11(nOUT_BUS_REGB), .pin12(nOUT_BUS_REGA), .pin13(nOUT_BUS_PC), .pin14(nOUT_BUS_RAM),
    .pin15(BUS_OUT_0), .pin16(1'b1));
  Seven_Seg #(.commonCathode("true"), .ledPersistence("true")) seven_seg_1 (
    .a(a), .b(b), .c(c), .d(d), .e(e), .f(f), .g(g), .dp(1'b0), .common(SIGN));
  Seven_Seg #(.commonCathode("true"), .ledPersistence("true")) seven_seg_2 (
    .a(a), .b(b), .c(c), .d(d), .e(e), .f(f), .g(g), .dp(1'b0), .common(_100s));
  and and_1 (OUT_1s, BUS_OUT_0, BUS_OUT_6, BUS_OUT_7);
  Seven_Seg #(.commonCathode("true"), .ledPersistence("true")) seven_seg_3 (
    .a(a), .b(b), .c(c), .d(d), .e(e), .f(f), .g(g), .dp(1'b0), .common(_10s));
  assign BUS = ~OUT_1s ? {8{1'b1}} : 8'bz;  // DriverInvSel driverinvsel_1
  Seven_Seg #(.commonCathode("true"), .ledPersistence("true")) seven_seg_4 (
    .a(a), .b(b), .c(c), .d(d), .e(e), .f(f), .g(g), .dp(1'b0), .common(_1s));

  // Notes on the sheet:
  //   CLOCK: Hz: 2
  //   CLOCK_OUT: Hz: 10
endmodule
